# Fritzing sketch Trike (saved by Fritzing 1.0.5)
# 18650 Li-ion Battery: CC-BY Dr Kristofer Chan, King's College London/Remote-research.org
perfboards: 1

parts:
  Componente2 = Bluetooth HC-05 Macho
  L298N2 = L298N DC motor driver
  BAT1 = 18650 Li-ion Battery [package=battery-18650]
  BAT2 = 18650 Li-ion Battery [package=battery-18650]
  BAT3 = 18650 Li-ion Battery [package=battery-18650]
  M3 = DC Motor [voltage_(max)=6V voltage_(min)=3V]
  M4 = DC Motor [voltage_(max)=6V voltage_(min)=3V]
  S1 = Toggle Switch [package=THT]
  J1 = Basic Servo
  Componente3 = Arduino Uno (Rev3) - ICSP

nets:
  N1: Componente2.TXD, Componente3.D2
  GND: Componente2.GND, Componente3.GND
  N2: L298N2.OUT1, M3.pin_2
  N3: L298N2.OUT2, M3.pin_1
  N4: L298N2.OUT3, M4.pin_2
  N5: L298N2.OUT4, M4.pin_1
  N6: L298N2.12V, S1.L2
  N7: L298N2.GND, BAT3.-
  N8: L298N2.ENA, Componente3.D9_PWM
  N9: L298N2.ENB, Componente3.D4
  N10: L298N2.IN1, Componente3.D5_PWM
  N11: L298N2.IN2, Componente3.D6_PWM
  N12: L298N2.IN3, Componente3.D7
  N13: L298N2.IN4, Componente3.D8
  N14: BAT1.-, BAT2.+
  N15: BAT1.+, S1.COM
  N16: BAT2.-, BAT3.+
  N17: J1.pulse, Componente3.D3_PWM

notes:
  FILTER
  IN
  OUT

custom parts:
  L298N DC motor driver: 2x DC motor driver with 78M05 positive voltage regulator (7..35 V) L298N: max 46 V, 2 A Set 5 V Enable jumper to enable 5 V regultor (needed for the L298N) and +5 V output at screw terminal or supply external +5 V at screw terminal Set ENA and/or ENB to +5 V to enable motor permanently or supply ENA and/or ENB with PWM signal IN1 and IN2 set rotation directory for motor A (OUT1/OUT2) IN2 and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
  18650 Li-ion Battery: 18650 li-ion Battery Standard 18650 battery with interactive connectors Creative Common Attribution 4.0 International (CC-BY 4.0) license. Any use of this part requires attribution of Dr Kristofer Chan, Department of Geography, King's College London. Contact kristofer.chan [at] kcl.ac.uk OR kris [at] remote-research.org for further information.
